// Logisim project 1.circ as structural Verilog: 2 circuits, main circuit main
module main (
);

  wire A, and_1_out, and_2_out, and_3_out, and_4_out, and_5_out, and_6_out, and_7_out, B, C, clock, D, f, g,
       go, not_1_out, not_2_out, not_3_out, not_4_out, not_5_out, Reset_out, t_ff_1_q, t_ff_2_q, t_ff_3_q,
       t_ff_4_q;

  not not_1 (not_1_out, A);
  // Probe on {A, B, C, D}
  Clock clock_1 (.out(clock));
  // Probe on {A, B, C, D}
  not not_2 (not_2_out, C);
  // Probe on f
  T_Flip_Flop t_ff_1 (.clk(clock), .T(1'b1), .Q(t_ff_1_q), .Qn(D), .preset(Reset_out), .en(go));  // open: reset
  // Probe on g
  not not_3 (not_3_out, D);
  TTY #(.rows(1), .cols(18)) tty_1 (.data({6'b011000, f}), .clk(clock), .we(go), .clr(Reset_out));
  T_Flip_Flop t_ff_2 (.clk(t_ff_3_q), .T(1'b1), .Q(t_ff_2_q), .Qn(B), .preset(Reset_out));  // open: reset, en
  T_Flip_Flop t_ff_3 (.clk(t_ff_1_q), .T(1'b1), .Q(t_ff_3_q), .Qn(C), .preset(Reset_out));  // open: reset, en
  TTY #(.rows(1), .cols(18)) tty_2 (.data({6'b011000, g}), .clk(clock), .we(go), .clr(Reset_out));
  and and_1 (and_1_out, B, not_2_out, not_3_out);
  and and_2 (and_2_out, not_1_out, B, D);
  and and_3 (and_3_out, not_1_out, B, C);
  and and_4 (and_4_out, A, B, C);
  T_Flip_Flop t_ff_4 (.clk(t_ff_2_q), .T(1'b1), .Q(t_ff_4_q), .Qn(A), .preset(Reset_out));  // open: reset, en
  T_Flip_Flop t_ff_5 (.clk(t_ff_4_q), .T(1'b1), .Q(go), .preset(Reset_out));  // open: Qn, reset, en
  or or_1 (f, and_1_out, and_2_out, and_3_out, and_4_out);
  Button Reset (.out(Reset_out));
  not not_4 (not_4_out, A);
  not not_5 (not_5_out, D);
  and and_5 (and_5_out, B, not_5_out);
  and and_6 (and_6_out, not_4_out, B);
  and and_7 (and_7_out, B, C);
  or or_2 (g, and_5_out, and_6_out, and_7_out);

  // Notes on the sheet:
  //   0000111100001011
  //   0000111100001011
endmodule

module test (
);

  main main_1 ();
endmodule
