// Logisim project 3.circ as structural Verilog: 1 circuit, main circuit main
module main (
);

  wire A, adder_1_cout, adder_1_out, adder_2_cout, adder_2_out, adder_3_cout, B, C, clock_1_out, D, E, F, go,
       Reset_out, t_ff_1_q, t_ff_2_q, t_ff_3_q, t_ff_4_q, t_ff_5_q, t_ff_6_q, X0, X1, X2;

  Adder #(.width(1)) adder_1 (.a(B), .b(C), .out(adder_1_out), .cin(A), .cout(adder_1_cout));
  Adder #(.width(1)) adder_2 (.a(E), .b(F), .out(adder_2_out), .cin(D), .cout(adder_2_cout));
  // Probe on {A, B, C, D, E, F}
  // Probe on {X2, X1, X0}
  Clock clock_1 (.out(clock_1_out));
  Adder #(.width(1)) adder_3 (.a(adder_1_out), .b(adder_2_out), .out(X0), .cout(adder_3_cout));  // open: cin
  Adder #(.width(1)) adder_4 (.a(adder_1_cout), .b(adder_2_cout), .out(X1), .cin(adder_3_cout), .cout(X2));
  TTY #(.rows(1), .cols(65)) tty_1 (.data({4'b0110, X2, X1, X0}), .clk(clock_1_out), .we(go), .clr(Reset_out));
  T_Flip_Flop t_ff_1 (.clk(clock_1_out), .T(1'b1), .Q(t_ff_1_q), .Qn(F), .preset(Reset_out), .en(go));  // open: reset
  T_Flip_Flop t_ff_2 (.clk(t_ff_1_q), .T(1'b1), .Q(t_ff_2_q), .Qn(E), .preset(Reset_out));  // open: reset, en
  T_Flip_Flop t_ff_3 (.clk(t_ff_2_q), .T(1'b1), .Q(t_ff_3_q), .Qn(D), .preset(Reset_out));  // open: reset, en
  T_Flip_Flop t_ff_4 (.clk(t_ff_3_q), .T(1'b1), .Q(t_ff_4_q), .Qn(C), .preset(Reset_out));  // open: reset, en
  T_Flip_Flop t_ff_5 (.clk(t_ff_4_q), .T(1'b1), .Q(t_ff_5_q), .Qn(B), .preset(Reset_out));  // open: reset, en
  T_Flip_Flop t_ff_6 (.clk(t_ff_5_q), .T(1'b1), .Q(t_ff_6_q), .Qn(A), .preset(Reset_out));  // open: reset, en
  T_Flip_Flop t_ff_7 (.clk(t_ff_6_q), .T(1'b1), .Q(go), .preset(Reset_out));  // open: Qn, reset, en
  Button Reset (.out(Reset_out));

  // Notes on the sheet:
  //   0112122312232334122323342334344512232334233434452334344534454556
endmodule
