// Logisim project 2.circ as structural Verilog: 1 circuit, main circuit main
module main (
);

  wire _4_Counter_carry, CLK, clock_1_out, go, Q, R, Reset_out, RQ_out, S, S_nQ_out, t_ff_1_qn, T_out;
  wire [3:0] _4_Counter_q;

  and S_nQ (S_nQ_out, Q, R);
  and RQ (RQ_out, S, t_ff_1_qn);
  TTY #(.rows(1), .cols(12)) tty_1 (.data({6'b011000, Q}), .clk(CLK), .we(go), .clr(Reset_out));
  or T (T_out, S_nQ_out, RQ_out);
  Button Reset (.out(Reset_out));
  T_Flip_Flop t_ff_1 (.clk(CLK), .T(T_out), .Q(Q), .Qn(t_ff_1_qn));  // open: preset, reset, en
  // Probe on _4_Counter_q
  Counter #(.width(4), .max('hc)) _4_Counter (
    .Q(_4_Counter_q), .carry(_4_Counter_carry), .clk(CLK), .clr(Reset_out));  // open: load, D, count
  and and_1 (CLK, clock_1_out, go);
  Clock clock_1 (.out(clock_1_out));
  not not_1 (go, _4_Counter_carry);
  ROM #(.addrWidth(4), .dataWidth(2)) rom_1 (.addr(_4_Counter_q), .data({R, S}));  // open: sel
  // Probe on S
  // Probe on R

  // Notes on the sheet:
  //   001111000011
  //   contents of rom_1 (hex, n*v repeats v):
  //   0 1 0 1 0 2 0 2 0 1
endmodule
