// Logisim project 3.circ as structural Verilog: 1 circuit, main circuit main
module main (
);

  wire _4_Counter_carry, CLK, clock_1_out, d_ff_1_qn, go, J, J_nQ_out, K, nKQ_out, not_1_out, or_1_out, Q,
       Reset_out;
  wire [3:0] _4_Counter_q;

  not not_1 (not_1_out, K);
  and J_nQ (J_nQ_out, d_ff_1_qn, J);
  and nKQ (nKQ_out, not_1_out, Q);
  TTY #(.rows(1), .cols(16)) tty_1 (.data({6'b011000, Q}), .clk(CLK), .we(go), .clr(Reset_out));
  or or_1 (or_1_out, J_nQ_out, nKQ_out);
  Button Reset (.out(Reset_out));
  Clock clock_1 (.out(clock_1_out));
  // Probe on _4_Counter_q
  Counter #(.width(4), .max('hf)) _4_Counter (
    .Q(_4_Counter_q), .carry(_4_Counter_carry), .clk(CLK), .clr(Reset_out));  // open: load, D, count
  and and_1 (CLK, clock_1_out, go);
  D_Flip_Flop d_ff_1 (.clk(CLK), .D(or_1_out), .Q(Q), .Qn(d_ff_1_qn));  // open: preset, en, reset
  not not_2 (go, _4_Counter_carry);
  // Probe on J
  ROM #(.addrWidth(4), .dataWidth(2)) rom_1 (.addr(_4_Counter_q), .data({K, J}));  // open: sel
  // Probe on K

  // Notes on the sheet:
  //   001100111101000
  //   contents of rom_1 (hex, n*v repeats v):
  //   0 1 0 2 0 3 0 1 1 2 1 3 2 2 3 3
endmodule
