// Logisim project 4.circ as structural Verilog: 1 circuit, main circuit main
module main (
);

  wire and_1_out, and_2_out, and_3_out, and_6_out, and_7_out, and_8_out, and_9_out, and_10_out, and_11_out,
       and_12_out, and_13_out, and_14_out, and_15_out, and_16_out, and_17_out, and_18_out, and_19_out,
       and_20_out, and_21_out, Carry, CLK, clock_1_out, counter_1_carry, D0, D1, D2, D3, Enable, Load,
       multiplexer_1_out, multiplexer_2_out, multiplexer_3_out, multiplexer_4_out, not_1_out, not_2_out,
       not_3_out, not_4_out, not_5_out, not_6_out, not_7_out, not_8_out, not_9_out, not_11_out, not_12_out,
       not_13_out, not_14_out, or_1_out, or_2_out, or_4_out, or_5_out, or_7_out, or_8_out, or_9_out,
       or_10_out, Q0, Q1, Q2, Q3, t_ff_1_qn, t_ff_2_qn, t_ff_3_qn, t_ff_4_qn;
  wire [5:1] counter_1_q;

  and and_1 (and_1_out, Enable, Q0);
  and and_2 (and_2_out, and_1_out, Q1);
  and and_3 (and_3_out, and_2_out, Q2);
  and and_4 (Carry, and_3_out, Q3);
  Counter #(.width(6), .max('h24)) counter_1 (
    .Q({counter_1_q[5], Load, D3, counter_1_q[2:1], D0}), .carry(counter_1_carry), .clk(CLK));  // open: load, D, count, clr
  and and_5 (CLK, clock_1_out, not_1_out);
  not not_1 (not_1_out, counter_1_carry);
  Clock clock_1 (.out(clock_1_out));
  not not_2 (not_2_out, Enable);
  and and_6 (and_6_out, not_2_out, Q0);
  not not_3 (not_3_out, Q0);
  and and_7 (and_7_out, not_3_out, Enable);
  not not_4 (not_4_out, and_1_out);
  not not_5 (not_5_out, Q1);
  not not_6 (not_6_out, and_2_out);
  not not_7 (not_7_out, Q2);
  not not_8 (not_8_out, and_3_out);
  not not_9 (not_9_out, Q3);
  TTY #(.rows(1), .cols(37)) tty_1 (.data({2'b10, Carry, Q3, Q2, Q1, Q0}), .clk(CLK));  // open: we, clr
  not not_10 (Enable, counter_1_q[5]);
  or or_1 (or_1_out, and_6_out, and_7_out);
  and and_8 (and_8_out, not_4_out, Q1);
  or or_2 (or_2_out, and_8_out, and_9_out);
  and and_9 (and_9_out, not_5_out, and_1_out);
  and and_10 (and_10_out, not_6_out, Q2);
  and and_11 (and_11_out, not_7_out, and_2_out);
  and and_12 (and_12_out, not_8_out, Q3);
  and and_13 (and_13_out, not_9_out, and_3_out);
  or or_3 (D1, Enable, counter_1_q[1]);
  Multiplexer #(.enable("false")) multiplexer_1 (.in0(or_1_out), .in1(D0), .out(multiplexer_1_out), .sel(Load));
  Multiplexer #(.enable("false")) multiplexer_2 (.in0(or_2_out), .in1(D1), .out(multiplexer_2_out), .sel(Load));
  or or_4 (or_4_out, and_10_out, and_11_out);
  Multiplexer #(.enable("false")) multiplexer_3 (.in0(or_4_out), .in1(D2), .out(multiplexer_3_out), .sel(Load));
  or or_5 (or_5_out, and_12_out, and_13_out);
  Multiplexer #(.enable("false")) multiplexer_4 (.in0(or_5_out), .in1(D3), .out(multiplexer_4_out), .sel(Load));
  not not_11 (not_11_out, multiplexer_1_out);
  not not_12 (not_12_out, multiplexer_2_out);
  not not_13 (not_13_out, multiplexer_3_out);
  not not_14 (not_14_out, multiplexer_4_out);
  or or_6 (D2, counter_1_q[2], Load);
  and and_14 (and_14_out, Q0, not_11_out);
  and and_15 (and_15_out, multiplexer_1_out, t_ff_1_qn);
  and and_16 (and_16_out, Q1, not_12_out);
  and and_17 (and_17_out, multiplexer_2_out, t_ff_2_qn);
  and and_18 (and_18_out, Q2, not_13_out);
  and and_19 (and_19_out, multiplexer_3_out, t_ff_3_qn);
  and and_20 (and_20_out, Q3, not_14_out);
  and and_21 (and_21_out, multiplexer_4_out, t_ff_4_qn);
  or or_7 (or_7_out, and_14_out, and_15_out);
  or or_8 (or_8_out, and_16_out, and_17_out);
  or or_9 (or_9_out, and_18_out, and_19_out);
  or or_10 (or_10_out, and_20_out, and_21_out);
  T_Flip_Flop t_ff_1 (.clk(CLK), .T(or_7_out), .Q(Q0), .Qn(t_ff_1_qn));  // open: preset, reset, en
  T_Flip_Flop t_ff_2 (.clk(CLK), .T(or_8_out), .Q(Q1), .Qn(t_ff_2_qn));  // open: preset, reset, en
  T_Flip_Flop t_ff_3 (.clk(CLK), .T(or_9_out), .Q(Q2), .Qn(t_ff_3_qn));  // open: preset, reset, en
  T_Flip_Flop t_ff_4 (.clk(CLK), .T(or_10_out), .Q(Q3), .Qn(t_ff_4_qn));  // open: preset, reset, en

  // Notes on the sheet:
  //   @ABCDEFGHIJKLMN_@FGFGFGFGN_N_N_N0000
endmodule
