// Logisim project 5.circ as structural Verilog: 1 circuit, main circuit main
module main (
);

  wire _4_Counter_carry, _8_Counter_carry, A_nW_out, AW_out, CLK, clock_1_out, go, nA_nB_out, nAW_out,
       not_1_out, not_2_out, not_3_out, Q, Reset_out, T1_out, T2_out, t_ff_1_q, t_ff_2_q, w;
  wire [1:0] _4_Counter_q;
  wire [3:0] _8_Counter_q;

  not not_1 (not_1_out, w);
  not not_2 (not_2_out, t_ff_1_q);
  TTY #(.rows(1), .cols(33)) tty_1 (.data({6'b011000, Q}), .clk(CLK), .we(go), .clr(Reset_out));
  and A_nW (A_nW_out, not_1_out, t_ff_2_q);
  and nAW (nAW_out, w, not_3_out);
  and nA_nB (nA_nB_out, not_3_out, not_2_out);
  and AW (AW_out, w, t_ff_2_q);
  and and_1 (CLK, clock_1_out, go);
  Clock clock_1 (.out(clock_1_out));
  or T1 (T1_out, A_nW_out, nAW_out);
  not not_3 (not_3_out, t_ff_2_q);
  or T2 (T2_out, nA_nB_out, AW_out);
  // Probe on _4_Counter_q
  Counter #(.width(2), .max('h3)) _4_Counter (
    .Q(_4_Counter_q), .carry(_4_Counter_carry), .clk(CLK), .clr(Reset_out));  // open: load, D, count
  T_Flip_Flop t_ff_1 (.clk(CLK), .T(T1_out), .Q(t_ff_1_q));  // open: Qn, preset, reset, en
  T_Flip_Flop t_ff_2 (.clk(CLK), .T(T2_out), .Q(t_ff_2_q));  // open: Qn, preset, reset, en
  Counter #(.width(4), .max('h8)) _8_Counter (
    .Q(_8_Counter_q), .carry(_8_Counter_carry), .clk(_4_Counter_carry), .clr(Reset_out));  // open: load, D, count
  // Probe on w
  // Probe on _8_Counter_q
  BitSelector #(.width(4)) bitselector_1 (.in(_8_Counter_q), .out(w), .sel(_4_Counter_q));
  not not_4 (go, _8_Counter_carry);
  Button Reset (.out(Reset_out));
  and and_2 (Q, t_ff_1_q, t_ff_2_q);

  // Notes on the sheet:
  //   Eight gates
  //   0010100000001000101000000100001
endmodule
