// Logisim project 6moore.circ as structural Verilog: 1 circuit, main circuit main
module main (
);

  wire _4_Counter_carry, A_q, A_qn, Aw_out, B_q, B_qn, BCDF_out, C_q, C_qn, CLK, clock_1_out, D_q, D_qn, E_q,
       E_qn, go, nA_nBC_nw_out, nA_nBCDEw_out, nA_nBE_nF_out, nA_nBE_nw_out, nA_nCDEw_out, nA_nCE_nF_out,
       nA_nCE_nw_out, nA_nDE_nF_out, nA_nDE_nw_out, nAB_nC_out, nAB_nD_out, nAB_nE_out, nAC_nD_out,
       nAC_nE_out, nAD_nE_out, nEw_out, not_1_out, or_1_out, or_2_out, or_3_out, or_4_out, Q, Reset_out, w;
  wire [1:0] _4_Counter_q;
  wire [3:0] _32_Counter_q_2;
  wire [4:4] _32_Counter_q;

  not not_1 (not_1_out, w);
  and nAB_nC (nAB_nC_out, A_qn, B_q, C_qn);
  and nAB_nD (nAB_nD_out, A_qn, B_q, D_qn);
  and nAB_nE (nAB_nE_out, A_qn, B_q, E_qn);
  and nAC_nD (nAC_nD_out, A_qn, C_q, D_qn);
  and nAC_nE (nAC_nE_out, A_qn, C_q, E_qn);
  and nA_nBC_nw (nA_nBC_nw_out, A_qn, B_qn, C_q, not_1_out);
  and nA_nCDEw (nA_nCDEw_out, A_qn, C_qn, D_q, E_q, w);
  and nAD_nE (nAD_nE_out, A_qn, D_q, E_qn);
  and nA_nBE_nw (nA_nBE_nw_out, A_qn, D_qn, E_q, w);
  and nA_nCE_nw (nA_nCE_nw_out, A_qn, B_qn, D_q, not_1_out);
  and nA_nDE_nw (nA_nDE_nw_out, A_qn, C_qn, D_q, not_1_out);
  and nEw (nEw_out, E_qn, w);
  and Aw (Aw_out, A_q, w);
  and nA_nBE_nF (nA_nBE_nF_out, A_qn, B_qn, E_q, not_1_out);
  and nA_nCE_nF (nA_nCE_nF_out, A_qn, C_qn, E_q, not_1_out);
  and nA_nDE_nF (nA_nDE_nF_out, A_qn, D_qn, E_q, not_1_out);
  and BCDF (BCDF_out, B_q, C_q, D_q, w);
  and nA_nBCDEw (nA_nBCDEw_out, A_qn, B_qn, C_q, D_q, E_q, w);
  or or_1 (or_1_out, nAB_nC_out, nAB_nD_out, nAB_nE_out, nA_nBCDEw_out);
  or or_2 (or_2_out, nAC_nD_out, nAC_nE_out, nA_nBC_nw_out, nA_nCDEw_out);
  or or_3 (or_3_out, nAD_nE_out, nA_nBE_nw_out, nA_nCE_nw_out, nA_nDE_nw_out);
  or or_4 (or_4_out, nEw_out, Aw_out, nA_nBE_nF_out, nA_nCE_nF_out, nA_nDE_nF_out, BCDF_out);
  D_Flip_Flop A (.clk(CLK), .D(or_1_out), .Q(A_q), .Qn(A_qn));  // open: preset, en, reset
  D_Flip_Flop B (.clk(CLK), .D(or_2_out), .Q(B_q), .Qn(B_qn));  // open: preset, en, reset
  D_Flip_Flop C (.clk(CLK), .D(or_3_out), .Q(C_q), .Qn(C_qn));  // open: preset, en, reset
  D_Flip_Flop D (.clk(CLK), .D(or_4_out), .Q(D_q), .Qn(D_qn));  // open: preset, en, reset
  D_Flip_Flop E (.clk(CLK), .D(not_1_out), .Q(E_q), .Qn(E_qn));  // open: preset, en, reset
  and A_nBC_nE (Q, A_q, B_qn, C_q, E_qn);
  Clock clock_1 (.out(clock_1_out));
  TTY #(.rows(17), .cols(4)) tty_1 (.data({6'b011000, Q}), .clk(CLK), .we(go), .clr(Reset_out));
  Button Reset (.out(Reset_out));
  Counter #(.width(2), .max('h3)) _4_Counter (
    .Q(_4_Counter_q), .carry(_4_Counter_carry), .clk(CLK), .clr(Reset_out));  // open: load, D, count
  and and_1 (CLK, clock_1_out, go);
  Counter #(.width(5), .max('h1f), .trigger("falling")) _32_Counter (
    .Q({_32_Counter_q[4], _32_Counter_q_2}), .clk(_4_Counter_carry), .clr(Reset_out));  // open: load, D, count, carry
  // Probe on _4_Counter_q
  // Probe on _32_Counter_q_2
  not not_2 (go, _32_Counter_q[4]);
  // Probe on w
  BitSelector #(.width(4)) bitselector_1 (.in(_32_Counter_q_2), .out(w), .sel(_4_Counter_q));

  // Notes on the sheet:
  //   13 gates
  //   0000
  //   1000
  //   0100
  //   1100
  //   0010
  //   1010
  //   0110
  //   1110
  //   0001
  //   1001
  //   0101
  //   1101
  //   0011
  //   1011
  //   0111
  //   1111
  //   1
  //   1
endmodule
