// Logisim project 8.circ as structural Verilog: 1 circuit, main circuit main
module main (
);

  wire _4_Counter_carry, A_q, A_qn, and_1_out, and_2_out, and_3_out, and_4_out, and_5_out, and_6_out,
       and_7_out, and_8_out, and_9_out, and_10_out, and_11_out, and_12_out, B_q, B_qn, C_q, C_qn, CLK,
       clock_1_out, go, I5, I10, I25, not_1_out, not_2_out, O5, O10, OM, or_4_out, or_5_out, or_6_out,
       Reset_out;
  wire [4:0] _4_Counter_q;

  not not_1 (not_1_out, I5);
  not not_2 (not_2_out, I25);
  and and_1 (and_1_out, not_1_out, A_q);
  and and_2 (and_2_out, I25, C_q);
  and and_3 (and_3_out, I25, A_q);
  and and_4 (and_4_out, I25, B_q);
  and and_5 (and_5_out, not_1_out, C_q, B_q);
  and and_6 (and_6_out, B_q, C_qn, I10);
  and and_7 (and_7_out, B_q, C_q, I5);
  and and_8 (and_8_out, A_qn, B_qn, I10);
  and and_9 (and_9_out, B_qn, C_q, not_2_out);
  and and_10 (and_10_out, B_q, C_qn, I5);
  and and_11 (and_11_out, A_qn, C_qn, I5);
  and and_12 (and_12_out, B_qn, C_q, I10);
  or or_1 (O5, and_1_out, and_2_out);
  or or_2 (O10, and_3_out, and_4_out);
  or or_3 (OM, I25, A_q, and_5_out);
  or or_4 (or_4_out, and_6_out, and_7_out);
  or or_5 (or_5_out, and_8_out, and_9_out, and_10_out);
  or or_6 (or_6_out, and_11_out, and_12_out);
  D_Flip_Flop A (.clk(CLK), .D(or_4_out), .Q(A_q), .Qn(A_qn));  // open: preset, en, reset
  D_Flip_Flop B (.clk(CLK), .D(or_5_out), .Q(B_q), .Qn(B_qn));  // open: preset, en, reset
  D_Flip_Flop C (.clk(CLK), .D(or_6_out), .Q(C_q), .Qn(C_qn));  // open: preset, en, reset
  TTY #(.rows(1), .cols(33)) tty_1 (.data({4'b1000, OM, O10, O5}), .clk(CLK), .we(go), .clr(Reset_out));
  Button Reset (.out(Reset_out));
  Counter #(.width(5), .max('h1f)) _4_Counter (
    .Q(_4_Counter_q), .carry(_4_Counter_carry), .clk(CLK), .clr(Reset_out));  // open: load, D, count
  and and_13 (CLK, clock_1_out, go);
  Clock clock_1 (.out(clock_1_out));
  // Probe on _4_Counter_q
  not not_3 (go, _4_Counter_carry);
  ROM #(.addrWidth(5), .dataWidth(3)) rom_1 (.addr(_4_Counter_q), .data({I25, I10, I5}));  // open: sel
  // Probe on I10
  // Probe on I5
  // Probe on I25

  // Notes on the sheet:
  //   E
  //   F
  //   D
  //   24 Gates
  //   D@@@@D@@@D@@E@E@F@@G@@G@F@@E@@@
  //   contents of rom_1 (hex, n*v repeats v):
  //   4 6*1 2 1 1 2 2 2 1 4 2 4 2 2 4 1 2 4 2 4 2 2 2 1 1 1 2
endmodule
