// Logisim project alu.circ as structural Verilog: 3 circuits, main circuit main
module main (
);

  wire A0, A1, A2, A3, A4, B0, B1, B2, B3, B4, C0, C1, C1in, C2, C2in, C3, C3in, C4, C4in, C5, CIN,
       clock_1_out, clock_2_out, G0, G1, G2, G3, G4, go, HCLK, not_1_out, P0, P1, P2, P3, P4, reset, S0, S1;
  wire [2:0] multiplexer_1_out;
  wire [6:1] counter_1_q;

  _1b_ALU u_1b_alu_1 (.A(A0), .B(B0), .Cin(CIN), .G(G0), .C(C0), .P(P0), .in_4({S1, S0}));
  _1b_ALU u_1b_alu_2 (.A(A1), .B(B1), .Cin(C1in), .G(G1), .C(C1), .P(P1), .in_4({S1, S0}));
  _1b_ALU u_1b_alu_3 (.A(A2), .B(B2), .Cin(C2in), .G(G2), .C(C2), .P(P2), .in_4({S1, S0}));
  _1b_ALU u_1b_alu_4 (.A(A3), .B(B3), .Cin(C3in), .G(G3), .C(C3), .P(P3), .in_4({S1, S0}));
  _1b_ALU u_1b_alu_5 (.A(A4), .B(B4), .Cin(C4in), .G(G4), .C(C4), .P(P4), .in_4({S1, S0}));
  CLA cla_1 (
    .G0(G0), .G1(G1), .G2(G2), .G3(G3), .G4(G4), .P0(P0), .P1(P1), .P2(P2), .P3(P3), .P4(P4), .Cin(CIN),
    .C1in(C1in), .C2in(C2in), .C3in(C3in), .C4in(C4in), .C5(C5));
  // Probe on {C5, C4, C3}
  // Probe on {4'b0110, multiplexer_1_out}
  // Probe on {C2, C1, C0}
  Multiplexer #(.width(3)) multiplexer_1 (
    .in0({C5, C4, C3}), .in1({C2, C1, C0}), .out(multiplexer_1_out), .sel(HCLK));  // open: en
  // Probe on multiplexer_1_out
  TTY #(.rows(32), .cols(2)) tty_1 (.data({4'b0110, multiplexer_1_out}), .clk(clock_1_out), .we(go), .clr(reset));
  Clock clock_1 (.out(clock_1_out));
  // Probe on {A4, A3, A2, A1, A0, CIN}
  // Probe on {B4, B3, B2, B1, B0}
  // Probe on S1
  Counter #(.width(7), .max('h7f), .ongoal("stay")) counter_1 (
    .Q({counter_1_q, HCLK}), .clk(clock_2_out), .clr(reset));  // open: load, D, count, carry
  Clock clock_2 (.out(clock_2_out));
  // Probe on S0
  Button u_Reset (.out(reset));
  not not_1 (not_1_out, HCLK);
  Random #(.width(13), .seed(34573)) random_1 (
    .clk(not_1_out), .next(go), .out({B4, B3, B2, B1, B0, A4, A3, A2, A1, A0, CIN, S1, S0}), .clr(reset));
  not not_2 (go, counter_1_q[6]);

  // Other names for the same wires on the sheet: Sel[1:0] = {S1, S0}

  // Notes on the sheet:
  //   07
  //   51
  //   40
  //   51
  //   77
  //   77
  //   57
  //   63
  //   43
  //   77
  //   60
  //   51
  //   46
  //   71
  //   32
  //   43
  //   34
  //   50
  //   53
  //   00
  //   07
  //   02
  //   74
  //   04
  //   35
  //   52
  //   52
  //   50
  //   65
  //   46
  //   11
  //   57
endmodule

module _1b_ALU (
  input  A,
  input  B,
  input  Cin,
  input  [1:0] in_4,
  output G,
  output C,
  output P
);

  wire not_1_out, xor_1_out, xor_2_out;

  and and_1 (G, A, B);
  or or_1 (P, A, B);
  not not_1 (not_1_out, A);
  xor xor_1 (xor_1_out, A, B);
  xor xor_2 (xor_2_out, xor_1_out, Cin);
  Multiplexer #(.select(2), .enable("false")) multiplexer_1 (
    .in0(G), .in1(P), .in2(not_1_out), .in3(xor_2_out), .out(C), .sel(in_4));
endmodule

module CLA (
  input  G0,
  input  G1,
  input  G2,
  input  G3,
  input  G4,
  input  P0,
  input  P1,
  input  P2,
  input  P3,
  input  P4,
  input  Cin,
  output C1in,
  output C2in,
  output C3in,
  output C4in,
  output C5
);

  wire and_1_out, and_2_out, and_3_out, and_4_out, and_5_out, and_6_out, and_7_out, and_8_out, and_9_out,
       P0C0_out, P1G0_out, P1P0C0_out, P2G1_out, P2P1G0_out, P2P1P0C0_out;

  and P0C0 (P0C0_out, P0, Cin);
  and P1P0C0 (P1P0C0_out, P1, P0, Cin);
  and P1G0 (P1G0_out, P1, G0);
  and P2G1 (P2G1_out, P2, G1);
  and P2P1G0 (P2P1G0_out, P2, P1, G0);
  and P2P1P0C0 (P2P1P0C0_out, P2, P1, P0, Cin);
  and and_1 (and_1_out, Cin, P0, P1, P2, P3);
  and and_2 (and_2_out, G0, P1, P2, P3);
  and and_3 (and_3_out, G1, P2, P3);
  and and_4 (and_4_out, G2, P3);
  and and_5 (and_5_out, Cin, P0, P1, P2, P3, P4);
  and and_6 (and_6_out, G0, P1, P2, P3, P4);
  and and_7 (and_7_out, G1, P2, P3, P4);
  and and_8 (and_8_out, G2, P3, P4);
  and and_9 (and_9_out, G3, P4);
  or or_1 (C1in, P0C0_out, G0);
  or or_2 (C2in, P1P0C0_out, P1G0_out, G1);
  or or_3 (C3in, P2G1_out, P2P1G0_out, P2P1P0C0_out, G2);
  or or_4 (C4in, and_1_out, and_2_out, and_3_out, and_4_out, G3);
  or or_5 (C5, and_5_out, and_6_out, and_7_out, and_8_out, and_9_out, G4);
endmodule
