// Logisim project CPUtest.circ as structural Verilog: 8 circuits, main circuit main
module main (
  output [9:0] out_1,
  output [9:0] out_2,
  output [9:0] out_3,
  output [9:0] out_4,
  output [9:0] out_5,
  output [9:0] out_6,
  output [9:0] out_7,
  output ignore,
  output halt
);

  wire and_1_out, CLK, clock_1_out, comparator_1_lt, comparator_2_lt, decoder_1_out7, DEnable, not_1_out,
       PCSel, t_ff_1_q, TClock;
  wire [1:0] counter_2_q, Upper_2_bits;
  wire [2:0] ASel, B, DSel, rom_1_data;
  wire [3:0] BSel;
  wire [4:0] adder_1_out, counter_1_q, multiplexer_1_out, OPCode, undriven, undriven_2;
  wire [6:0] adder_2_out, adder_3_out, ASCII, decoder_1_out0, LSB, MiddleBits;
  wire [7:0] multiplexer_4_out;
  wire [9:0] Data, multiplexer_2_out, multiplexer_3_out, registerbank_1_r0, registerbank_1_r1,
       registerbank_1_r2, registerbank_1_r3, registerbank_1_r4, registerbank_1_r5, registerbank_1_r6,
       undriven_3;

  PCRegister pcregister_1 ();  // open: DataIn, CLK, WE, DataOut
  // Probe on nothing
  Adder #(.width(5)) adder_1 (.a(multiplexer_1_out), .b(undriven_2), .out(adder_1_out));  // open: cin, cout
  PCRegister pcregister_2 ();  // open: DataIn, CLK, WE, DataOut
  Multiplexer #(.width(5), .enable("false")) multiplexer_1 (
    .in0({5{1'b1}}), .in1(Data[4:0]), .out(multiplexer_1_out), .sel(PCSel));
  RAM #(.addrWidth(5), .dataWidth(24), .bus("separate")) ram_1 (
    .addr(undriven), .data({OPCode, DSel, ASel, B, Data}));  // open: din, str, sel, clk, ld, clr
  Decoder #(.select(3)) decoder_1 (
    .out0(decoder_1_out0[0]), .out1(decoder_1_out0[1]), .out2(decoder_1_out0[2]), .out3(decoder_1_out0[3]),
    .out4(decoder_1_out0[4]), .out5(decoder_1_out0[5]), .out6(decoder_1_out0[6]), .out7(decoder_1_out7),
    .sel(DSel), .en(DEnable));
  Multiplexer #(.select(3), .width(10), .enable("false")) multiplexer_2 (
    .in0(registerbank_1_r0), .in1(registerbank_1_r1), .in2(registerbank_1_r2), .in3(registerbank_1_r3),
    .in4(registerbank_1_r4), .in5(registerbank_1_r5), .in6(registerbank_1_r6), .out(multiplexer_2_out),
    .sel(ASel));  // open: in7
  TTY #(.rows(33), .cols(4)) tty_1 (.data(ASCII), .clk(TClock));  // open: we, clr
  // Probe on out_1
  Counter #(.width(5), .max('h1f), .ongoal("stay")) counter_1 (
    .Q(counter_1_q), .carry(halt), .clk(CLK));  // open: load, D, count, clr
  Multiplexer #(.select(4), .width(10), .enable("false")) multiplexer_3 (
    .in0(registerbank_1_r0), .in1(registerbank_1_r1), .in2(registerbank_1_r2), .in3(registerbank_1_r3),
    .in4(registerbank_1_r4), .in5(registerbank_1_r5), .in6(registerbank_1_r6), .in7({10{1'b0}}), .in8(Data),
    .out(multiplexer_3_out), .sel(BSel));  // open: in9, in10, in11, in12, in13, in14, in15
  // Probe on out_5
  Multiplexer #(.select(3), .width(10)) multiplexer_4 (
    .in0(out_1), .in1(out_2), .in2(out_3), .in3(out_4), .in4(out_5), .in5(out_6), .in6(out_7),
    .out({Upper_2_bits, multiplexer_4_out}), .sel(rom_1_data));  // open: in7, en
  not not_1 (not_1_out, halt);
  Clock clock_1 (.out(clock_1_out));
  // Probe on out_2
  // Probe on out_6
  and and_1 (and_1_out, not_1_out, clock_1_out);
  RegisterBank registerbank_1 (
    .CLK(CLK), .DataIn(undriven_3), .R0(registerbank_1_r0), .R1(registerbank_1_r1), .R2(registerbank_1_r2),
    .R3(registerbank_1_r3), .R4(registerbank_1_r4), .R5(registerbank_1_r5), .R6(registerbank_1_r6),
    .WA(decoder_1_out0));
  // Probe on out_3
  // Probe on out_7
  ROM #(.addrWidth(5), .dataWidth(3)) rom_1 (.addr(counter_1_q), .data(rom_1_data));  // open: sel
  not not_2 (TClock, and_1_out);
  // Probe on out_4
  Comparator #(.width(7)) comparator_1 (
    .a(7'b0111001), .b({3'b011, multiplexer_4_out[3:0]}), .lt(comparator_1_lt));  // open: gt, eq
  Comparator #(.width(7)) comparator_2 (
    .a(7'b0111001), .b({3'b011, multiplexer_4_out[7:4]}), .lt(comparator_2_lt));  // open: gt, eq
  T_Flip_Flop t_ff_1 (.clk(and_1_out), .T(1'b1), .Q(t_ff_1_q));  // open: Qn, preset, reset, en
  Adder #(.width(7)) adder_2 (
    .a({3'b011, multiplexer_4_out[3:0]}), .b(7'b0000111), .out(adder_2_out));  // open: cin, cout
  Adder #(.width(7)) adder_3 (
    .a({3'b011, multiplexer_4_out[7:4]}), .b(7'b0000111), .out(adder_3_out));  // open: cin, cout
  Multiplexer #(.select(2), .width(7)) multiplexer_5 (
    .in0({5'b01100, Upper_2_bits}), .in1(MiddleBits), .in2(LSB), .in3(7'b0100000), .out(ASCII),
    .sel(counter_2_q));  // open: en
  Counter #(.width(2), .max('h3)) counter_2 (.Q(counter_2_q), .clk(TClock));  // open: load, D, count, carry, clr
  T_Flip_Flop t_ff_2 (.clk(t_ff_1_q), .T(1'b1), .Q(CLK));  // open: Qn, preset, reset, en
  Multiplexer #(.width(7), .disabled(0), .enable("false")) multiplexer_6 (
    .in0({3'b011, multiplexer_4_out[3:0]}), .in1(adder_2_out), .out(LSB), .sel(comparator_1_lt));
  Multiplexer #(.width(7), .disabled(0), .enable("false")) multiplexer_7 (
    .in0({3'b011, multiplexer_4_out[7:4]}), .in1(adder_3_out), .out(MiddleBits), .sel(comparator_2_lt));
  T_Flip_Flop t_ff_3 (.clk(CLK), .T(1'b1), .Q(ignore));  // open: Qn, preset, reset, en

  // Other names for the same wires on the sheet: R0[9:0] = out_1; R1[9:0] = out_2; R2[9:0] = out_3; R3[9:0] = out_4;
  //   R4[9:0] = out_5; R5[9:0] = out_6; R6[9:0] = out_7

  // Notes on the sheet:
  //   DO NOT PUT ANY PINS ON THE main circuit.  (You should not need any anyway.)
  //   0F5
  //   0F5
  //   25A
  //   050
  //   2FF
  //   30A
  //   34F
  //   0F5
  //   1EA
  //   07A
  //   29B
  //   165
  //   10F
  //   0F5
  //   0AA
  //   0AA
  //   05A
  //   00A
  //   0FA
  //   104
  //   0B4
  //   165
  //   165
  //   001
  //   001
  //   000
  //   000
  //   000
  //   000
  //   000
  //   ???
  //   There is no Reset.  Just Ctrl-r, then load test.txt into your RAM, and then Ctrl-k
  //   You must  use the CLK tunnel for the source of your clock.  R0-R6 are the other tunnels you need to connect
  //   contents of rom_1 (hex, n*v repeats v):
  //   0 0 0 1 2 3 4 5 6 2 3 4 5 6 0 0 0 1 3 4 6 3 5 5 8*6
endmodule

module Register (
  input  CLK,
  input  WE,
  input  [9:0] DataOut,
  input  [9:0] DataIn
);

  D_Flip_Flop d_ff_1 (.clk(CLK), .D(DataIn[0]), .Q(DataOut[0]), .en(WE));  // open: Qn, preset, reset
  D_Flip_Flop d_ff_2 (.clk(CLK), .D(DataIn[1]), .Q(DataOut[1]), .en(WE));  // open: Qn, preset, reset
  D_Flip_Flop d_ff_3 (.clk(CLK), .D(DataIn[2]), .Q(DataOut[2]), .en(WE));  // open: Qn, preset, reset
  D_Flip_Flop d_ff_4 (.clk(CLK), .D(DataIn[3]), .Q(DataOut[3]), .en(WE));  // open: Qn, preset, reset
  D_Flip_Flop d_ff_5 (.clk(CLK), .D(DataIn[4]), .Q(DataOut[4]), .en(WE));  // open: Qn, preset, reset
  D_Flip_Flop d_ff_6 (.clk(CLK), .D(DataIn[5]), .Q(DataOut[5]), .en(WE));  // open: Qn, preset, reset
  D_Flip_Flop d_ff_7 (.clk(CLK), .D(DataIn[6]), .Q(DataOut[6]), .en(WE));  // open: Qn, preset, reset
  D_Flip_Flop d_ff_8 (.clk(CLK), .D(DataIn[7]), .Q(DataOut[7]), .en(WE));  // open: Qn, preset, reset
  D_Flip_Flop d_ff_9 (.clk(CLK), .D(DataIn[8]), .Q(DataOut[8]), .en(WE));  // open: Qn, preset, reset
  D_Flip_Flop d_ff_10 (.clk(CLK), .D(DataIn[9]), .Q(DataOut[9]), .en(WE));  // open: Qn, preset, reset
endmodule

module RegisterBank (
  input  [6:0] WA,
  input  CLK,
  input  [9:0] DataIn,
  output [9:0] R0,
  output [9:0] R1,
  output [9:0] R2,
  output [9:0] R3,
  output [9:0] R4,
  output [9:0] R5,
  output [9:0] R6
);

  Register register_1 (.DataIn(DataIn), .CLK(CLK), .WE(WA[6]), .DataOut(R6));
  Register register_2 (.DataIn(DataIn), .CLK(CLK), .WE(WA[5]), .DataOut(R5));
  Register register_3 (.DataIn(DataIn), .CLK(CLK), .WE(WA[3]), .DataOut(R3));
  Register register_4 (.DataIn(DataIn), .CLK(CLK), .WE(WA[4]), .DataOut(R4));
  Register register_5 (.DataIn(DataIn), .CLK(CLK), .WE(WA[2]), .DataOut(R2));
  Register register_6 (.DataIn(DataIn), .CLK(CLK), .WE(WA[1]), .DataOut(R1));
  Register register_7 (.DataIn(DataIn), .CLK(CLK), .WE(WA[0]), .DataOut(R0));
endmodule

module PCRegister (
  input  CLK,
  input  WE,
  input  [4:0] DataOut,
  input  [4:0] DataIn
);

  D_Flip_Flop d_ff_1 (.clk(CLK), .D(DataIn[0]), .Q(DataOut[0]), .en(WE));  // open: Qn, preset, reset
  D_Flip_Flop d_ff_2 (.clk(CLK), .D(DataIn[1]), .Q(DataOut[1]), .en(WE));  // open: Qn, preset, reset
  D_Flip_Flop d_ff_3 (.clk(CLK), .D(DataIn[2]), .Q(DataOut[2]), .en(WE));  // open: Qn, preset, reset
  D_Flip_Flop d_ff_4 (.clk(CLK), .D(DataIn[3]), .Q(DataOut[3]), .en(WE));  // open: Qn, preset, reset
  D_Flip_Flop d_ff_5 (.clk(CLK), .D(DataIn[4]), .Q(DataOut[4]), .en(WE));  // open: Qn, preset, reset
endmodule

module ALU (
  input  [3:0] Sel,
  input  [9:0] AIn,
  input  Cin,
  input  [9:0] BIn,
  output [9:0] Out
);

  wire C10, Cin1, Cin2, Cin3, Cin4, Cin5, Cin6, Cin7, Cin8, Cin9, G0, G1, G2, G3, G4, G5, G6, G7, G8, G9, P0,
       P1, P2, P3, P4, P5, P6, P7, P8, P9;
  wire [1:0] undriven;

  _1bit_ALU u_1bit_alu_1 (.C(Out[0]), .A(AIn[0]), .B(BIn[0]), .Cin(Cin), .G(G0), .P(P0), .ALUControl(undriven));
  _1bit_ALU u_1bit_alu_2 (.C(Out[1]), .A(AIn[1]), .B(BIn[1]), .Cin(Cin1), .G(G1), .P(P1), .ALUControl(undriven));
  _1bit_ALU u_1bit_alu_3 (.C(Out[2]), .A(AIn[2]), .B(BIn[2]), .Cin(Cin2), .G(G2), .P(P2), .ALUControl(undriven));
  _1bit_ALU u_1bit_alu_4 (.C(Out[3]), .A(AIn[3]), .B(BIn[3]), .Cin(Cin3), .G(G3), .P(P3), .ALUControl(undriven));
  _1bit_ALU u_1bit_alu_5 (.C(Out[4]), .A(AIn[4]), .B(BIn[4]), .Cin(Cin4), .G(G4), .P(P4), .ALUControl(undriven));
  _1bit_ALU u_1bit_alu_6 (.C(Out[5]), .A(AIn[5]), .B(BIn[5]), .Cin(Cin5), .G(G5), .P(P5), .ALUControl(undriven));
  _1bit_ALU u_1bit_alu_7 (.C(Out[6]), .A(AIn[6]), .B(BIn[6]), .Cin(Cin6), .G(G6), .P(P6), .ALUControl(undriven));
  _1bit_ALU u_1bit_alu_8 (.C(Out[7]), .A(AIn[7]), .B(BIn[7]), .Cin(Cin7), .G(G7), .P(P7), .ALUControl(undriven));
  _1bit_ALU u_1bit_alu_9 (.C(Out[8]), .A(AIn[8]), .B(BIn[8]), .Cin(Cin8), .G(G8), .P(P8), .ALUControl(undriven));
  _1bit_ALU u_1bit_alu_10 (.C(Out[9]), .A(AIn[9]), .B(BIn[9]), .Cin(Cin9), .G(G9), .P(P9), .ALUControl(undriven));
  CLA cla_1 (
    .Cin1(Cin1), .Cin2(Cin2), .Cin3(Cin3), .Cin4(Cin4), .C5(Cin5), .G0(G0), .G1(G1), .G2(G2), .G3(G3),
    .G4(G4), .P0(P0), .P1(P1), .P2(P2), .P3(P3), .P4(P4));  // open: Cin
  CLA cla_2 (
    .Cin1(Cin6), .Cin2(Cin7), .Cin3(Cin8), .Cin4(Cin9), .C5(C10), .G0(G5), .G1(G6), .G2(G7), .G3(G8),
    .G4(G9), .P0(P5), .P1(P6), .P2(P7), .P3(P8), .P4(P9), .Cin(Cin5));

  // Other names for the same wires on the sheet: A0 = AIn[0]; A1 = AIn[1]; A2 = AIn[2]; A3 = AIn[3]; A4 = AIn[4];
  //   A5 = AIn[5]; A6 = AIn[6]; A7 = AIn[7]; A8 = AIn[8]; A9 = AIn[9]; B0 = BIn[0]; B1 = BIn[1]; B2 = BIn[2];
  //   B3 = BIn[3]; B4 = BIn[4]; B5 = BIn[5]; B6 = BIn[6]; B7 = BIn[7]; B8 = BIn[8]; B9 = BIn[9]; C0 = Out[0];
  //   C1 = Out[1]; C2 = Out[2]; C3 = Out[3]; C4 = Out[4]; C5 = Out[5]; C6 = Out[6]; C7 = Out[7]; C8 = Out[8];
  //   C9 = Out[9]; sub = Sel[3]
endmodule

module ControlUnit (
  input  [2:0] B,
  input  [4:0] OPCode,
  input  [2:0] B_2,
  input  CLK,
  input  ZeroFlag,
  output [3:0] ALUControl,
  output [2:0] BSel,
  output PCSel,
  output DecoderEnable,
  output PCCLK
);

  wire decoder_1_out7, decoder_1_out9, decoder_1_out11, decoder_1_out12, decoder_1_out15, not_2_out, NZ;
  wire [3:0] undriven;

  not not_1 (NZ, ZeroFlag);
  Multiplexer #(.select(4), .width(3), .enable("false")) multiplexer_1 (
    .in0(3'b000), .in1(3'b001), .in2(3'b010), .in3(3'b011), .in4(3'b100), .in5(3'b101), .in6(3'b110),
    .in7(3'b011), .in8(3'b011), .in9(3'b011), .in10(3'b111), .in11(3'b111), .in12(3'b100), .in13(3'b100),
    .out(ALUControl[2:0]), .sel(undriven));  // open: in14, in15
  Multiplexer #(.select(4), .width(3), .enable("false")) multiplexer_2 (
    .out(BSel), .sel(undriven));  // open: in0, in1, in2, in3, in4, in5, in6, in7, in8, in9, in10, in11, in12, in13, in14, in15
  Decoder #(.select(4), .enable("false")) decoder_1 (
    .out7(decoder_1_out7), .out9(decoder_1_out9), .out11(decoder_1_out11), .out12(decoder_1_out12),
    .out15(decoder_1_out15), .sel(OPCode[3:0]));  // open: out0, out1, out2, out3, out4, out5, out6, out8, out10, out13, out14
  or SUB (ALUControl[3], decoder_1_out7, decoder_1_out9);
  not not_2 (not_2_out, decoder_1_out15);
  and BNEZ (PCSel, NZ, decoder_1_out11);
  and HALT (PCCLK, not_2_out, CLK);
  nor nor_1 (DecoderEnable, decoder_1_out11, decoder_1_out12, decoder_1_out15);
endmodule

module CLA (
  input  G0,
  input  G1,
  input  G2,
  input  G3,
  input  G4,
  input  P0,
  input  P1,
  input  P2,
  input  P3,
  input  P4,
  input  Cin,
  output Cin1,
  output Cin2,
  output Cin3,
  output Cin4,
  output C5
);

  wire and_1_out, and_2_out, and_3_out, and_4_out, and_5_out, and_6_out, and_7_out, and_8_out, and_9_out,
       P0C0_out, P1G0_out, P1P0C0_out, P2G1_out, P2P1G0_out, P2P1P0C0_out;

  and P0C0 (P0C0_out, P0, Cin);
  and P1P0C0 (P1P0C0_out, P1, P0, Cin);
  and P1G0 (P1G0_out, P1, G0);
  and P2G1 (P2G1_out, P2, G1);
  and P2P1G0 (P2P1G0_out, P2, P1, G0);
  and P2P1P0C0 (P2P1P0C0_out, P2, P1, P0, Cin);
  and and_1 (and_1_out, Cin, P0, P1, P2, P3);
  and and_2 (and_2_out, G0, P1, P2, P3);
  and and_3 (and_3_out, G1, P2, P3);
  and and_4 (and_4_out, G2, P3);
  and and_5 (and_5_out, Cin, P0, P1, P2, P3, P4);
  and and_6 (and_6_out, G0, P1, P2, P3, P4);
  and and_7 (and_7_out, G1, P2, P3, P4);
  and and_8 (and_8_out, G2, P3, P4);
  and and_9 (and_9_out, G3, P4);
  or or_1 (Cin1, P0C0_out, G0);
  or or_2 (Cin2, P1P0C0_out, P1G0_out, G1);
  or or_3 (Cin3, P2G1_out, P2P1G0_out, P2P1P0C0_out, G2);
  or or_4 (Cin4, and_1_out, and_2_out, and_3_out, and_4_out, G3);
  or or_5 (C5, and_5_out, and_6_out, and_7_out, and_8_out, and_9_out, G4);
endmodule

module _1bit_ALU (
  input  A,
  input  B,
  input  Cin,
  input  [1:0] ALUControl,
  output G,
  output P,
  output C
);

  wire not_1_out, xor_1_out, xor_2_out;

  and and_1 (G, A, B);
  or or_1 (P, A, B);
  not not_1 (not_1_out, A);
  xor xor_1 (xor_1_out, A, B);
  xor xor_2 (xor_2_out, xor_1_out, Cin);
  Multiplexer #(.select(2), .enable("false")) multiplexer_1 (
    .in0(G), .in1(P), .in2(not_1_out), .in3(xor_2_out), .out(C), .sel(ALUControl));
endmodule
